# Fritzing sketch DROduino v1.0 (saved by Fritzing 0.7.12b)
breadboards: 1

parts:
  Arduino1 = Arduino
  LCD1 = LCD screen
  R1 = Rotary Potentiometer (Small) [maximum_resistance=100kΩ]
  X_AXIS = Rotary Encoder [package=THT]
  Z_AXIS = Rotary Encoder [package=THT]
  IN/MM = Pushbutton [package="[THT]"]
  X-ZERO = Pushbutton [package="[THT]"]
  Z-ZERO = Pushbutton [package="[THT]"]
  R2 = Resistor [tolerance=±5% resistance=2.2k package=THT]
  R3 = Resistor [tolerance=±5% resistance=2.2k package=THT]
  R4 = Resistor [tolerance=±5% resistance=2.2k package=THT]

nets:
  N1: Arduino1.D12, LCD1.DB7
  N2: Arduino1.D11, LCD1.DB6
  N3: Arduino1.D10, LCD1.DB5
  N4: Arduino1.D9, LCD1.DB4
  N5: Arduino1.D8, LCD1.E
  N6: Arduino1.D7, LCD1.RS
  N7: Arduino1.D5, Z_AXIS.EncoderPinC
  N8: Arduino1.D4, X_AXIS.EncoderPinC
  N9: Arduino1.D3, Z_AXIS.EncoderPinA
  N10: Arduino1.D2, X_AXIS.EncoderPinA
  +5V: Arduino1.+5V, LCD1.VDD, LCD1.LED+, R1.leg2, X_AXIS.EncoderPinB, Z_AXIS.EncoderPinB, IN/MM.Pin_3, IN/MM.Pin_4, X-ZERO.Pin_3, X-ZERO.Pin_4, Z-ZERO.Pin_3, Z-ZERO.Pin_4
  GND: Arduino1.GND, LCD1.VSS, LCD1.R/W, LCD1.LED-, R1.leg1, R2.Pin_0, R3.Pin_0, R4.Pin_0
  N11: Arduino1.A0, IN/MM.Pin_1, IN/MM.Pin_2, R2.Pin_1
  N12: Arduino1.A1, X-ZERO.Pin_1, X-ZERO.Pin_2, R3.Pin_1
  N13: Arduino1.A2, Z-ZERO.Pin_1, Z-ZERO.Pin_2, R4.Pin_1
  N14: LCD1.V0, R1.wiper
